// Logisim project Lab11.circ as structural Verilog
module Output (
  input  x,
  input  w,
  input  y,
  input  z,
  output a,
  output b,
  output c,
  output d
);

  wire and_1_out, and_2_out, and_3_out, and_4_out, and_5_out, and_6_out, and_7_out, and_8_out, and_9_out,
       and_10_out, and_11_out, and_12_out, and_13_out, not_1_out, not_2_out, not_3_out, not_4_out, not_5_out,
       not_6_out, not_7_out, not_8_out, not_9_out, not_10_out, not_11_out, not_12_out, not_13_out, not_14_out;

  and and_1 (and_1_out, w, y, z);
  and and_2 (and_2_out, x, z);
  and and_3 (and_3_out, x, y);
  and and_4 (and_4_out, x, w);
  not not_1 (not_1_out, x);
  not not_2 (not_2_out, w);
  not not_3 (not_3_out, x);
  not not_4 (not_4_out, y);
  not not_5 (not_5_out, z);
  not not_6 (not_6_out, w);
  not not_7 (not_7_out, y);
  not not_8 (not_8_out, z);
  not not_9 (not_9_out, x);
  not not_10 (not_10_out, y);
  and and_5 (and_5_out, not_9_out, not_10_out, z);
  not not_11 (not_11_out, x);
  and and_6 (and_6_out, not_11_out, y, not_12_out);
  not not_12 (not_12_out, z);
  and and_7 (and_7_out, x, not_13_out, not_14_out);
  not not_13 (not_13_out, y);
  not not_14 (not_14_out, z);
  and and_8 (and_8_out, x, y, z);
  not not_15 (d, z);
  or or_1 (a, and_1_out, and_2_out, and_3_out, and_4_out);
  and and_9 (and_9_out, not_1_out, not_2_out, y, z);
  and and_10 (and_10_out, not_3_out, w, not_4_out);
  and and_11 (and_11_out, w, y, not_5_out);
  and and_12 (and_12_out, x, not_6_out, not_7_out, not_8_out);
  and and_13 (and_13_out, x, w, z);
  or or_2 (c, and_5_out, and_6_out, and_7_out, and_8_out);
  or or_3 (b, and_9_out, and_10_out, and_11_out, and_12_out, and_13_out);
endmodule
