// Logisim project lab10.circ as structural Verilog: 1 circuit, main circuit main
module main (
  input  X,
  input  Y,
  input  Z
);

  wire and_1_out, not_1_out, not_2_out, not_3_out, or_1_out, or_2_out, X_prime_Y_prime_out,
       X_prime_Y_prime_Z_2_out, X_prime_Y_prime_Z_out, X_prime_Y_prime_Z_prime_out, X_prime_YZ_2_out,
       X_prime_YZ_out, X_prime_YZ_prime_2_out, X_prime_YZ_prime_3_out, X_prime_YZ_prime_out, XYZ_out, YZ_out;

  not not_1 (not_1_out, X);
  not not_2 (not_2_out, Z);
  not not_3 (not_3_out, Y);
  and X_prime_Y_prime (X_prime_Y_prime_out, not_1_out, not_3_out);
  and YZ (YZ_out, Y, Z);
  and X_prime_YZ_prime (X_prime_YZ_prime_out, not_1_out, Y, not_2_out);
  and X_prime_Y_prime_Z_prime (X_prime_Y_prime_Z_prime_out, not_1_out, not_3_out, not_2_out);
  and X_prime_Y_prime_Z (X_prime_Y_prime_Z_out, not_1_out, not_3_out, Z);
  and X_prime_YZ_prime_2 (X_prime_YZ_prime_2_out, not_1_out, Y, not_2_out);
  and X_prime_YZ (X_prime_YZ_out, not_1_out, Y, Z);
  and XYZ (XYZ_out, X, Y, Z);
  or X_prime_YZ_2 (X_prime_YZ_2_out, not_1_out, Y, Z);
  or X_prime_YZ_prime_3 (X_prime_YZ_prime_3_out, not_1_out, Y, not_2_out);
  or X_prime_Y_prime_Z_2 (X_prime_Y_prime_Z_2_out, not_1_out, not_3_out, Z);
  or or_1 (or_1_out, X_prime_Y_prime_out, YZ_out, X_prime_YZ_prime_out);
  or or_2 (or_2_out, X_prime_Y_prime_Z_prime_out, X_prime_Y_prime_Z_out, X_prime_YZ_prime_2_out, X_prime_YZ_out, XYZ_out);
  and and_1 (and_1_out, X_prime_YZ_2_out, X_prime_YZ_prime_3_out, X_prime_Y_prime_Z_2_out);
  LED led_1 (.in(or_1_out));
  LED led_2 (.in(or_2_out));
  LED led_3 (.in(and_1_out));
endmodule
