// Logisim project lab11b.circ as structural Verilog: 1 circuit, main circuit main
module main (
  input  A3,
  input  A2,
  input  A1,
  input  A0,
  input  B3,
  input  B2,
  input  B1,
  input  B0,
  output out_9,
  output S4,
  output S3,
  output S2,
  output S1,
  output S0
);

  wire and_1_out, and_2_out, and_3_out, and_4_out, and_5_out, and_6_out, and_7_out, and_8_out, and_9_out,
       and_10_out, or_1_out, or_2_out, xor_1_out, xor_4_out, xor_6_out;

  and and_1 (and_1_out, B0, A0);
  xor xor_1 (xor_1_out, B1, A1);
  xor xor_2 (S0, B0, A0);
  and and_2 (and_2_out, B1, A1);
  and and_3 (and_3_out, and_1_out, B1);
  and and_4 (and_4_out, and_1_out, A1);
  xor xor_3 (S1, and_1_out, xor_1_out);
  or or_1 (or_1_out, and_2_out, and_3_out, and_4_out);
  xor xor_4 (xor_4_out, B2, A2);
  and and_5 (and_5_out, B2, A2);
  and and_6 (and_6_out, or_1_out, A2);
  and and_7 (and_7_out, or_1_out, B2);
  xor xor_5 (S2, or_1_out, xor_4_out);
  xor xor_6 (xor_6_out, B3, A3);
  or or_2 (or_2_out, and_5_out, and_6_out, and_7_out);
  xor xor_7 (S3, or_2_out, xor_6_out);
  and and_8 (and_8_out, B3, A3);
  and and_9 (and_9_out, or_2_out, B3);
  and and_10 (and_10_out, or_2_out, A3);
  or or_3 (S4, and_8_out, and_9_out, and_10_out);
endmodule
