// Logisim project lab12a.circ as structural Verilog: 1 circuit, main circuit main
module main (
  input  A,
  input  in_2,
  input  C,
  input  D,
  input  Leap,
  output _28,
  output out_7,
  output _30,
  output out_9
);

  wire and_3_out, and_4_out, and_5_out, and_6_out, and_7_out, not_1_out, not_2_out, not_3_out, not_4_out,
       not_5_out;

  not not_1 (not_1_out, A);
  not not_2 (not_2_out, in_2);
  not not_3 (not_3_out, C);
  not not_4 (not_4_out, D);
  not not_5 (not_5_out, Leap);
  and and_1 (_28, not_1_out, not_2_out, C, not_4_out, not_5_out);
  and and_2 (out_7, not_1_out, not_2_out, C, not_4_out, Leap);
  and and_3 (and_3_out, not_1_out, in_2, not_4_out);
  and and_4 (and_4_out, A, not_2_out, D);
  and and_5 (and_5_out, not_1_out, D);
  and and_6 (and_6_out, A, not_3_out, not_4_out);
  and and_7 (and_7_out, A, not_2_out, not_4_out);
  or or_1 (_30, and_3_out, and_4_out);
  or or_2 (out_9, and_5_out, and_6_out, and_7_out);

  // Notes on the sheet:
  //   B
  //   29
  //   31
endmodule
