// Logisim project lab14b.circ as structural Verilog: 1 circuit, main circuit main
module main (
  input  in_1,
  output out_2,
  output out_3
);

  wire and_1_out, and_2_out, and_3_out, and_4_out, clock_1_out, not_1_out, not_2_out, not_3_out, or_1_out,
       or_2_out;

  not not_1 (not_1_out, in_1);
  not not_2 (not_2_out, out_2);
  not not_3 (not_3_out, out_3);
  and and_1 (and_1_out, in_1, not_2_out);
  and and_2 (and_2_out, out_2, out_3);
  and and_3 (and_3_out, in_1, not_3_out);
  and and_4 (and_4_out, not_2_out, out_3);
  or or_1 (or_1_out, and_1_out, and_2_out);
  or or_2 (or_2_out, and_3_out, and_4_out);
  Clock clock_1 (.out(clock_1_out));
  T_Flip_Flop t_ff_1 (.clk(clock_1_out), .T(or_1_out), .Q(out_2));  // open: Qn, preset, reset, en
  T_Flip_Flop t_ff_2 (.clk(clock_1_out), .T(or_2_out), .Q(out_3));  // open: Qn, preset, reset, en
endmodule
